// Digital circuit Calc_Clock.dig as structural Verilog
module Calc_Clock (
  input  CLK,
  input  nR,
  output n2Q,
  output n1Q,
  output _1Q,
  output _2Q,
  output C,
  output T
);

  wire not_1_out;

  not not_1 (not_1_out, CLK);
  // _74107 _74107_1: pin names not known; wires that end beside it: n2Q, not_1_out, _2Q, nR, _1Q, not_1_out, n1Q, nR, 1'b1, 1'b0, _1Q, n1Q, _2Q, n2Q
  nand nand_1 (T, not_1_out, n2Q, n1Q);
  nand nand_2 (C, _2Q, _1Q, not_1_out);
endmodule
