// Digital circuit Calc_Display.dig as structural Verilog
module Calc_Display (
  input  V10,
  input  N1,
  input  N4,
  input  N2,
  input  N8,
  input  nV9,
  input  V8,
  input  nV6,
  input  V7,
  input  nV5,
  input  nV4,
  input  nV3,
  input  nV2,
  input  nV1,
  input  nDP,
  input  nERR,
  input  B1,
  input  Cclk,
  input  nR
);

  wire _7447_1_p9, _7447_1_p10, _7447_1_p11, _7447_1_p12, _7447_1_p13, _7447_1_p14, _7447_1_p15,
       _74173_1_p13, _74173_1_p14, _74173_1_p15, _74173_1_p16, and_1_out, nand_1_out, not_1_out, not_2_out,
       not_3_out, not_4_out, not_5_out, not_6_out, not_7_out, not_8_out, not_9_out, not_10_out, not_11_out,
       not_12_out, not_13_out, or_1_out, or_2_out, or_3_out, or_4_out, or_5_out;

  or or_1 (or_1_out, B1, Cclk);
  not not_1 (not_1_out, nR);
  // _74173 _74173_1: pin names not known; wires that end beside it: N1, N2, N4, N8, or_1_out, not_1_out, 1'b0, 1'b0, 1'b0, 1'b0, 1'b1, 1'b0, _74173_1_p13, _74173_1_p14, _74173_1_p15, _74173_1_p16
  // _7447 _7447_1: pin names not known; wires that end beside it: 1'b1, 1'b0, _74173_1_p13, _74173_1_p14, _74173_1_p15, _74173_1_p16, 1'b1, 1'b1, _7447_1_p9, _7447_1_p10, _7447_1_p11, _7447_1_p12, _7447_1_p13, _7447_1_p14, _7447_1_p15
  not not_2 (not_2_out, _7447_1_p12);
  nand nand_1 (nand_1_out, not_2_out, _7447_1_p15, nERR);
  or or_2 (or_2_out, nERR, nDP);
  and and_1 (and_1_out, _7447_1_p15, nand_1_out);
  not not_3 (not_3_out, nand_1_out);
  or or_3 (or_3_out, _7447_1_p10, not_3_out);
  or or_4 (or_4_out, _7447_1_p9, not_3_out);
  or or_5 (or_5_out, _7447_1_p14, not_3_out);
  Seven_Seg #(.commonCathode("true"), .commonConnectionType("anode")) seven_seg_1 (
    .a(or_4_out), .b(or_3_out), .c(_7447_1_p11), .d(_7447_1_p12), .e(_7447_1_p13), .f(or_5_out),
    .g(and_1_out), .dp(1'b1), .common(not_4_out));
  not not_4 (not_4_out, V10);
  not not_5 (not_5_out, nV9);
  not not_6 (not_6_out, V8);
  not not_7 (not_7_out, V7);
  not not_8 (not_8_out, nV6);
  not not_9 (not_9_out, nV5);
  not not_10 (not_10_out, nV4);
  not not_11 (not_11_out, nV3);
  not not_12 (not_12_out, nV2);
  not not_13 (not_13_out, nV1);
  Seven_Seg #(.commonCathode("true"), .commonConnectionType("anode")) seven_seg_2 (
    .a(or_4_out), .b(or_3_out), .c(_7447_1_p11), .d(_7447_1_p12), .e(_7447_1_p13), .f(or_5_out),
    .g(and_1_out), .dp(1'b1), .common(not_5_out));
  Seven_Seg #(.commonCathode("true"), .commonConnectionType("anode")) seven_seg_3 (
    .a(or_4_out), .b(or_3_out), .c(_7447_1_p11), .d(_7447_1_p12), .e(_7447_1_p13), .f(or_5_out),
    .g(and_1_out), .dp(1'b1), .common(not_6_out));
  Seven_Seg #(.commonCathode("true"), .commonConnectionType("anode")) seven_seg_4 (
    .a(or_4_out), .b(or_3_out), .c(_7447_1_p11), .d(_7447_1_p12), .e(_7447_1_p13), .f(or_5_out),
    .g(and_1_out), .dp(1'b1), .common(not_7_out));
  Seven_Seg #(.commonCathode("true"), .commonConnectionType("anode")) seven_seg_5 (
    .a(or_4_out), .b(or_3_out), .c(_7447_1_p11), .d(_7447_1_p12), .e(_7447_1_p13), .f(or_5_out),
    .g(and_1_out), .dp(1'b1), .common(not_8_out));
  Seven_Seg #(.commonCathode("true"), .commonConnectionType("anode")) seven_seg_6 (
    .a(or_4_out), .b(or_3_out), .c(_7447_1_p11), .d(_7447_1_p12), .e(_7447_1_p13), .f(or_5_out),
    .g(and_1_out), .dp(or_2_out), .common(not_9_out));
  Seven_Seg #(.commonCathode("true"), .commonConnectionType("anode")) seven_seg_7 (
    .a(or_4_out), .b(or_3_out), .c(_7447_1_p11), .d(_7447_1_p12), .e(_7447_1_p13), .f(or_5_out),
    .g(and_1_out), .dp(or_2_out), .common(not_10_out));
  Seven_Seg #(.commonCathode("true"), .commonConnectionType("anode")) seven_seg_8 (
    .a(or_4_out), .b(or_3_out), .c(_7447_1_p11), .d(_7447_1_p12), .e(_7447_1_p13), .f(or_5_out),
    .g(and_1_out), .dp(or_2_out), .common(not_11_out));
  Seven_Seg #(.commonCathode("true"), .commonConnectionType("anode")) seven_seg_9 (
    .a(or_4_out), .b(or_3_out), .c(_7447_1_p11), .d(_7447_1_p12), .e(_7447_1_p13), .f(or_5_out),
    .g(and_1_out), .dp(or_2_out), .common(not_12_out));
  Seven_Seg #(.commonCathode("true"), .commonConnectionType("anode")) seven_seg_10 (
    .a(or_4_out), .b(or_3_out), .c(_7447_1_p11), .d(_7447_1_p12), .e(_7447_1_p13), .f(or_5_out),
    .g(and_1_out), .dp(or_2_out), .common(not_13_out));
endmodule
