// Digital circuit Calc_Timing.dig as structural Verilog
module Calc_Timing (
  input  clk,
  output nB4,
  output B8,
  output nB8,
  output B1,
  output nB1,
  output nB2,
  output Cclk,
  output Tclk,
  output D0,
  output nD0,
  output nV1,
  output nV2,
  output nV3,
  output nV4,
  output nV5,
  output nV6,
  output nV7,
  output nV8,
  output nV9,
  output nV9_2,
  output nV11
);

  wire and_1_out, m5812_1_acout, m5812_2_acout, not_1_out, not_3_out;

  Calc_Clock calc_clock_1 (.CLK(clk), .nR(1'b1), .C(Cclk), .T(Tclk));  // open: n2Q, n1Q, _1Q, _2Q
  MS_DtypeFF ms_dtypeff_1 (.nCclk(Cclk), .nTclk(Tclk), .Din(nB2), .nR(1'b1), .Q(nB4));
  not not_1 (not_1_out, nB4);
  and and_1 (and_1_out, m5812_2_acout, m5812_1_acout);
  MS_DtypeFF ms_dtypeff_2 (.nCclk(Cclk), .nTclk(Tclk), .Din(not_1_out), .nR(1'b1), .Q(B8));
  M5812 m5812_1 (
    .ACin(m5812_2_acout), .Cclk(Cclk), .Tclk(Tclk), .D1(and_1_out), .Q1(nD0), .Q2(nV1), .Q3(nV2), .Q4(nV3),
    .Q5(nV4), .Q6(nV5), .ACout(m5812_1_acout));
  M5812 m5812_2 (
    .ACin(1'b1), .Cclk(Cclk), .Tclk(Tclk), .D1(not_3_out), .Q1(nV6), .Q2(nV7), .Q3(nV8), .Q4(nV9),
    .Q5(nV9_2), .Q6(nV11), .ACout(m5812_2_acout));
  not not_2 (nB8, B8);
  not not_3 (not_3_out, nV5);
  MS_DtypeFF ms_dtypeff_3 (.nCclk(Cclk), .nTclk(Tclk), .Din(B8), .nR(1'b1), .Q(B1));
  not not_4 (D0, nD0);
  or or_1 (nB2, not_1_out, B8, B1);
  not not_5 (nB1, B1);
endmodule
