// Digital circuit M5811 5bit state reg.dig as structural Verilog
module M5811_5bit_state_reg (
  input  nRQin,
  input  Cclk,
  input  Tclk,
  input  D1,
  input  D2,
  input  D3,
  input  D4,
  input  D5,
  output nRQout,
  output Q1,
  output Q2,
  output Q3,
  output Q4,
  output Q5
);

  wire and_1_out;

  MS_DtypeFF ms_dtypeff_1 (.nCclk(Cclk), .nTclk(Tclk), .Din(D1), .nR(1'b1), .Q(Q1));
  MS_DtypeFF ms_dtypeff_2 (.nCclk(Cclk), .nTclk(Tclk), .Din(D2), .nR(1'b1), .Q(Q2));
  MS_DtypeFF ms_dtypeff_3 (.nCclk(Cclk), .nTclk(Tclk), .Din(D3), .nR(1'b1), .Q(Q3));
  MS_DtypeFF ms_dtypeff_4 (.nCclk(Cclk), .nTclk(Tclk), .Din(D4), .nR(1'b1), .Q(Q4));
  MS_DtypeFF ms_dtypeff_5 (.nCclk(Cclk), .nTclk(Tclk), .Din(D5), .nR(1'b1), .Q(Q5));
  and and_1 (and_1_out, D1, D2, D3);
  and and_2 (nRQout, and_1_out, D4, D5, nRQin);
endmodule
