// Digital circuit M5812.dig as structural Verilog
module M5812 (
  input  ACin,
  input  Cclk,
  input  Tclk,
  input  D1,
  output Q1,
  output Q2,
  output Q3,
  output Q4,
  output Q5,
  output Q6,
  output ACout
);

  wire and_1_out, ms_dtypeff_1_q, ms_dtypeff_2_q, ms_dtypeff_3_q, ms_dtypeff_4_q, ms_dtypeff_5_q,
       ms_dtypeff_6_q, not_1_out, not_8_out, not_9_out, not_10_out, not_11_out, not_12_out;

  MS_DtypeFF ms_dtypeff_1 (.nCclk(Cclk), .nTclk(Tclk), .Din(D1), .nR(1'b1), .Q(ms_dtypeff_1_q));
  MS_DtypeFF ms_dtypeff_2 (.nCclk(Cclk), .nTclk(Tclk), .Din(ms_dtypeff_1_q), .nR(1'b1), .Q(ms_dtypeff_2_q));
  MS_DtypeFF ms_dtypeff_3 (.nCclk(Cclk), .nTclk(Tclk), .Din(ms_dtypeff_2_q), .nR(1'b1), .Q(ms_dtypeff_3_q));
  MS_DtypeFF ms_dtypeff_4 (.nCclk(Cclk), .nTclk(Tclk), .Din(ms_dtypeff_3_q), .nR(1'b1), .Q(ms_dtypeff_4_q));
  MS_DtypeFF ms_dtypeff_5 (.nCclk(Cclk), .nTclk(Tclk), .Din(ms_dtypeff_4_q), .nR(1'b1), .Q(ms_dtypeff_5_q));
  MS_DtypeFF ms_dtypeff_6 (.nCclk(Cclk), .nTclk(Tclk), .Din(ms_dtypeff_5_q), .nR(1'b1), .Q(ms_dtypeff_6_q));
  not not_1 (not_1_out, ms_dtypeff_6_q);
  not not_2 (Q1, ms_dtypeff_1_q);
  not not_3 (Q2, ms_dtypeff_2_q);
  not not_4 (Q3, ms_dtypeff_3_q);
  not not_5 (Q4, ms_dtypeff_4_q);
  not not_6 (Q5, ms_dtypeff_5_q);
  not not_7 (Q6, ms_dtypeff_6_q);
  not not_8 (not_8_out, ms_dtypeff_5_q);
  not not_9 (not_9_out, ms_dtypeff_4_q);
  not not_10 (not_10_out, ms_dtypeff_2_q);
  not not_11 (not_11_out, ms_dtypeff_3_q);
  not not_12 (not_12_out, ms_dtypeff_1_q);
  and and_1 (and_1_out, not_12_out, not_10_out, not_11_out);
  and and_2 (ACout, and_1_out, not_9_out, not_8_out, not_1_out, ACin);

  // Notes on the sheet:
  //   Ring Counter Shift Register
endmodule
