// Digital circuit M58211 serial BCD ADDER.dig as structural Verilog
module M58211_serial_BCD_ADDER (
  input  A,
  input  B,
  input  B8,
  input  CLK,
  input  CSUP,
  input  A_B,
  output N8,
  output N2,
  output N1,
  output N4,
  output COUT,
  output [3:0] hex
);

  wire and_1_out, and_2_out, and_3_out, and_4_out, and_5_out, and_6_out, and_7_out, CCLK, ms_dtypeff_4_q,
       ms_dtypeff_6_q, ms_dtypeff_7_q, ms_dtypeff_8_q, not_1_out, not_2_out, or_1_out, or_2_out, or_3_out,
       or_4_out, or_5_out, or_6_out, TCLK, xor_1_out, xor_2_out, xor_3_out, xor_4_out, xor_5_out;

  Calc_Clock calc_clock_1 (.CLK(CLK), .nR(1'b1), .C(CCLK), .T(TCLK));  // open: n2Q, n1Q, _1Q, _2Q
  not not_1 (not_1_out, CSUP);
  and and_1 (and_1_out, not_1_out, COUT);
  xor xor_1 (xor_1_out, A, A_B);
  or or_1 (or_1_out, B, and_1_out);
  xor xor_2 (xor_2_out, A, B);
  and and_2 (and_2_out, xor_1_out, or_1_out);
  and and_3 (and_3_out, B, and_1_out);
  xor xor_3 (xor_3_out, xor_2_out, and_1_out);
  or or_2 (or_2_out, and_2_out, and_3_out);
  MS_DtypeFF ms_dtypeff_1 (.Din(xor_3_out), .nCclk(CCLK), .nTclk(TCLK), .nR(1'b0), .Q(hex[3]));
  or or_3 (or_3_out, hex[2], hex[3]);
  MS_DtypeFF ms_dtypeff_2 (.Din(hex[3]), .nCclk(CCLK), .nTclk(TCLK), .nR(1'b0), .Q(hex[2]));
  and and_4 (and_4_out, or_3_out, xor_3_out, B8);
  MS_DtypeFF ms_dtypeff_3 (.Din(hex[2]), .nCclk(CCLK), .nTclk(TCLK), .nR(1'b0), .Q(hex[1]));
  or or_4 (or_4_out, and_4_out, or_2_out);
  MS_DtypeFF ms_dtypeff_4 (.Din(hex[1]), .nCclk(CCLK), .nTclk(TCLK), .nR(1'b0), .Q(ms_dtypeff_4_q));
  MS_DtypeFF ms_dtypeff_5 (.Din(or_4_out), .nCclk(CCLK), .nTclk(TCLK), .nR(1'b0), .Q(COUT));
  MS_DtypeFF ms_dtypeff_6 (.Din(B8), .nCclk(CCLK), .nTclk(TCLK), .nR(1'b0), .Q(ms_dtypeff_6_q));
  and and_5 (and_5_out, ms_dtypeff_6_q, COUT);
  or or_5 (or_5_out, ms_dtypeff_7_q, and_5_out);
  MS_DtypeFF ms_dtypeff_7 (.Din(or_5_out), .nCclk(CCLK), .nTclk(TCLK), .nR(B8), .Q(ms_dtypeff_7_q));
  xor xor_4 (xor_4_out, ms_dtypeff_4_q, ms_dtypeff_7_q);
  xor xor_5 (xor_5_out, ms_dtypeff_4_q, A_B);
  and and_6 (and_6_out, xor_5_out, ms_dtypeff_7_q);
  and and_7 (and_7_out, ms_dtypeff_8_q, not_2_out);
  not not_2 (not_2_out, B8);
  xor xor_6 (hex[0], xor_4_out, ms_dtypeff_8_q);
  or or_6 (or_6_out, and_6_out, and_7_out);
  MS_DtypeFF ms_dtypeff_8 (.Din(or_6_out), .nCclk(CCLK), .nTclk(TCLK), .nR(1'b0), .Q(ms_dtypeff_8_q));

  assign N1 = hex[0];
  assign N2 = hex[1];
  assign N4 = hex[2];
  assign N8 = hex[3];

  // Notes on the sheet:
  //   disables carry propogation
  //   used in division to suppress borrow
  //   Carry Generation
  //   ainv
  //   b+c
  //   Sum
  //   abc
  //   b*c
  //   carry
  //   n8 + n4
  //   Tens Carry
  //   tc
  //   cfd
  //   Carry Flag
  //   corrrection
  //   sixd
  //   SIX Generator
  //   Normalisation Adder
  //   NSINV
  //   NS ^ 6
  //   NSS
  //   Normalisation
  //   Carry Flag
endmodule
