// Digital circuit MC14517.dig as structural Verilog
module MC14517 (
  input  D,
  input  clk,
  output _48
);

  wire d_ff_1_q, d_ff_2_q, d_ff_3_q, d_ff_4_q, d_ff_5_q, d_ff_6_q, d_ff_7_q, d_ff_8_q, d_ff_9_q, d_ff_10_q,
       d_ff_11_q, d_ff_12_q, d_ff_13_q, d_ff_14_q, d_ff_15_q, d_ff_16_q, d_ff_17_q, d_ff_18_q, d_ff_19_q,
       d_ff_20_q, d_ff_21_q, d_ff_22_q, d_ff_23_q, d_ff_24_q, d_ff_25_q, d_ff_26_q, d_ff_27_q, d_ff_28_q,
       d_ff_29_q, d_ff_30_q, d_ff_31_q, d_ff_32_q, d_ff_33_q, d_ff_34_q, d_ff_35_q, d_ff_36_q, d_ff_37_q,
       d_ff_38_q, d_ff_39_q, d_ff_40_q, d_ff_41_q, d_ff_42_q, d_ff_43_q, d_ff_44_q, d_ff_45_q, d_ff_46_q,
       d_ff_48_q;

  D_FF d_ff_1 (.D(D), .C(clk), .Q(d_ff_1_q));  // open: nQ
  D_FF d_ff_2 (.D(d_ff_48_q), .C(clk), .Q(d_ff_2_q));  // open: nQ
  D_FF d_ff_3 (.D(d_ff_46_q), .C(clk), .Q(d_ff_3_q));  // open: nQ
  D_FF d_ff_4 (.D(d_ff_1_q), .C(clk), .Q(d_ff_4_q));  // open: nQ
  D_FF d_ff_5 (.D(d_ff_2_q), .C(clk), .Q(d_ff_5_q));  // open: nQ
  D_FF d_ff_6 (.D(d_ff_3_q), .C(clk), .Q(d_ff_6_q));  // open: nQ
  D_FF d_ff_7 (.D(d_ff_4_q), .C(clk), .Q(d_ff_7_q));  // open: nQ
  D_FF d_ff_8 (.D(d_ff_5_q), .C(clk), .Q(d_ff_8_q));  // open: nQ
  D_FF d_ff_9 (.D(d_ff_6_q), .C(clk), .Q(d_ff_9_q));  // open: nQ
  D_FF d_ff_10 (.D(d_ff_8_q), .C(clk), .Q(d_ff_10_q));  // open: nQ
  D_FF d_ff_11 (.D(d_ff_9_q), .C(clk), .Q(d_ff_11_q));  // open: nQ
  D_FF d_ff_12 (.D(d_ff_7_q), .C(clk), .Q(d_ff_12_q));  // open: nQ
  D_FF d_ff_13 (.D(d_ff_12_q), .C(clk), .Q(d_ff_13_q));  // open: nQ
  D_FF d_ff_14 (.D(d_ff_10_q), .C(clk), .Q(d_ff_14_q));  // open: nQ
  D_FF d_ff_15 (.D(d_ff_11_q), .C(clk), .Q(d_ff_15_q));  // open: nQ
  D_FF d_ff_16 (.D(d_ff_13_q), .C(clk), .Q(d_ff_16_q));  // open: nQ
  D_FF d_ff_17 (.D(d_ff_14_q), .C(clk), .Q(d_ff_17_q));  // open: nQ
  D_FF d_ff_18 (.D(d_ff_15_q), .C(clk), .Q(d_ff_18_q));  // open: nQ
  D_FF d_ff_19 (.D(d_ff_16_q), .C(clk), .Q(d_ff_19_q));  // open: nQ
  D_FF d_ff_20 (.D(d_ff_17_q), .C(clk), .Q(d_ff_20_q));  // open: nQ
  D_FF d_ff_21 (.D(d_ff_18_q), .C(clk), .Q(d_ff_21_q));  // open: nQ
  D_FF d_ff_22 (.D(d_ff_20_q), .C(clk), .Q(d_ff_22_q));  // open: nQ
  D_FF d_ff_23 (.D(d_ff_21_q), .C(clk), .Q(d_ff_23_q));  // open: nQ
  D_FF d_ff_24 (.D(d_ff_19_q), .C(clk), .Q(d_ff_24_q));  // open: nQ
  D_FF d_ff_25 (.D(d_ff_24_q), .C(clk), .Q(d_ff_25_q));  // open: nQ
  D_FF d_ff_26 (.D(d_ff_22_q), .C(clk), .Q(d_ff_26_q));  // open: nQ
  D_FF d_ff_27 (.D(d_ff_23_q), .C(clk), .Q(d_ff_27_q));  // open: nQ
  D_FF d_ff_28 (.D(d_ff_25_q), .C(clk), .Q(d_ff_28_q));  // open: nQ
  D_FF d_ff_29 (.D(d_ff_26_q), .C(clk), .Q(d_ff_29_q));  // open: nQ
  D_FF d_ff_30 (.D(d_ff_27_q), .C(clk), .Q(d_ff_30_q));  // open: nQ
  D_FF d_ff_31 (.D(d_ff_28_q), .C(clk), .Q(d_ff_31_q));  // open: nQ
  D_FF d_ff_32 (.D(d_ff_29_q), .C(clk), .Q(d_ff_32_q));  // open: nQ
  D_FF d_ff_33 (.D(d_ff_30_q), .C(clk), .Q(d_ff_33_q));  // open: nQ
  D_FF d_ff_34 (.D(d_ff_32_q), .C(clk), .Q(d_ff_34_q));  // open: nQ
  D_FF d_ff_35 (.D(d_ff_33_q), .C(clk), .Q(d_ff_35_q));  // open: nQ
  D_FF d_ff_36 (.D(d_ff_31_q), .C(clk), .Q(d_ff_36_q));  // open: nQ
  D_FF d_ff_37 (.D(d_ff_36_q), .C(clk), .Q(d_ff_37_q));  // open: nQ
  D_FF d_ff_38 (.D(d_ff_34_q), .C(clk), .Q(d_ff_38_q));  // open: nQ
  D_FF d_ff_39 (.D(d_ff_35_q), .C(clk), .Q(d_ff_39_q));  // open: nQ
  D_FF d_ff_40 (.D(d_ff_37_q), .C(clk), .Q(d_ff_40_q));  // open: nQ
  D_FF d_ff_41 (.D(d_ff_38_q), .C(clk), .Q(d_ff_41_q));  // open: nQ
  D_FF d_ff_42 (.D(d_ff_39_q), .C(clk), .Q(d_ff_42_q));  // open: nQ
  D_FF d_ff_43 (.D(d_ff_40_q), .C(clk), .Q(d_ff_43_q));  // open: nQ
  D_FF d_ff_44 (.D(d_ff_41_q), .C(clk), .Q(d_ff_44_q));  // open: nQ
  D_FF d_ff_45 (.D(d_ff_42_q), .C(clk), .Q(d_ff_45_q));  // open: nQ
  D_FF d_ff_46 (.D(d_ff_44_q), .C(clk), .Q(d_ff_46_q));  // open: nQ
  D_FF d_ff_47 (.D(d_ff_45_q), .C(clk), .Q(_48));  // open: nQ
  D_FF d_ff_48 (.D(d_ff_43_q), .C(clk), .Q(d_ff_48_q));  // open: nQ

  // Notes on the sheet:
  //   48 bit Shift register
endmodule
