// Digital circuit MS DtypeFF.dig as structural Verilog
module MS_DtypeFF (
  input  nCclk,
  input  nTclk,
  input  Din,
  input  nR,
  output Q
);

  wire _7474_1_p6, not_1_out, not_2_out;

  not not_1 (not_1_out, nCclk);
  not not_2 (not_2_out, nTclk);
  // _7474 _7474_1: pin names not known; wires that end beside it: 1'b1, Din, not_1_out, nR, 1'b1, _7474_1_p6, not_2_out, nR, 1'b1, 1'b0, _7474_1_p6, Q

  // Notes on the sheet:
  //   Master Slave FF , Cclk Loads first FF 
  //   Tclk outputs data from 2nd FF
endmodule
